# Fritzing sketch neopixel-gravitation (saved by Fritzing 0.8.7b)
breadboards: 1

parts:
  Part1 = Arduino Uno (Rev3)
  Part2 = Triple Axis Accelerometer Breakout - ADXL335
  U1 = LIPO-2000mAh [package=lipo-2000]  # not connected
  neopixel1 = Neopixel Ring 16
  C1 = Electrolytic Capacitor [capacitance=1000µF package="300 mil [THT, electrolytic]"]
  R1 = Resistor [tolerance=±5% resistance=220 package=THT]

nets:
  N1: Part1.A0, Part2.XOUT
  N2: Part1.A1, Part2.YOUT
  N3: Part1.D2, R1.Pin_0
  GND: Part1.GND, Part2.GND, neopixel1.GND, C1.-
  VCC: Part1.VIN, Part2.VCC, neopixel1.VCC, C1.+
  N4: neopixel1.IN, R1.Pin_1

notes:
  boost level convertor 3V -> 5V here

custom parts:
  Neopixel Ring 16: Neopixel Ring x16
